// Logisim project My-PC.circ as structural Verilog
module and_or_latch (
  input  set,
  input  reset,
  output \output 
);

  wire not_1_out, or_1_out;

  or or_1 (or_1_out, \output , set);
  not not_1 (not_1_out, reset);
  and and_1 (\output , or_1_out, not_1_out);
endmodule

module gated_latch (
  input  data_input,
  input  write_enable,
  output data_output
);

  wire and_1_out, and_2_out, not_1_out;

  not not_1 (not_1_out, data_input);
  and and_1 (and_1_out, data_input, write_enable);
  and_or_latch and_or_latch_1 (.set(and_1_out), .reset(and_2_out), .\output (data_output));
  and and_2 (and_2_out, not_1_out, write_enable);
endmodule

module latch_cell (
  input  write_enable,
  input  data_in,
  input  row,
  input  column,
  input  read_enable,
  output data_out
);

  wire and_1_out, and_2_out, and_3_out, gated_latch_1_data_output;

  and and_1 (and_1_out, row, column);
  gated_latch gated_latch_1 (.data_input(data_in), .write_enable(and_2_out), .data_output(gated_latch_1_data_output));
  and and_2 (and_2_out, write_enable, and_1_out);
  and and_3 (and_3_out, and_1_out, read_enable);
  and and_4 (data_out, gated_latch_1_data_output, and_3_out);
endmodule

module latch_row (
  input  data_in,
  input  write_enable,
  input  row,
  input  read_enable,
  input  column_0,
  input  column_1,
  input  column_2,
  input  column_3,
  input  column_4,
  input  column_5,
  input  column_6,
  input  column_7,
  output data_out
);

  wire latch_cell_1_data_out, latch_cell_2_data_out, latch_cell_3_data_out, latch_cell_4_data_out,
       latch_cell_5_data_out, latch_cell_6_data_out, latch_cell_7_data_out, latch_cell_8_data_out;

  latch_cell latch_cell_1 (
    .row(row), .write_enable(write_enable), .data_in(data_in), .column(column_0), .read_enable(read_enable),
    .data_out(latch_cell_1_data_out));
  latch_cell latch_cell_2 (
    .row(row), .write_enable(write_enable), .data_in(data_in), .column(column_1), .read_enable(read_enable),
    .data_out(latch_cell_2_data_out));
  latch_cell latch_cell_3 (
    .row(row), .write_enable(write_enable), .data_in(data_in), .column(column_3), .read_enable(read_enable),
    .data_out(latch_cell_3_data_out));
  latch_cell latch_cell_4 (
    .row(row), .write_enable(write_enable), .data_in(data_in), .column(column_2), .read_enable(read_enable),
    .data_out(latch_cell_4_data_out));
  latch_cell latch_cell_5 (
    .row(row), .write_enable(write_enable), .data_in(data_in), .column(column_4), .read_enable(read_enable),
    .data_out(latch_cell_5_data_out));
  or or_1 (data_out, latch_cell_1_data_out, latch_cell_2_data_out, latch_cell_4_data_out, latch_cell_3_data_out, latch_cell_5_data_out, latch_cell_6_data_out, latch_cell_7_data_out, latch_cell_8_data_out);
  latch_cell latch_cell_6 (
    .row(row), .write_enable(write_enable), .data_in(data_in), .column(column_5), .read_enable(read_enable),
    .data_out(latch_cell_6_data_out));
  latch_cell latch_cell_7 (
    .row(row), .write_enable(write_enable), .data_in(data_in), .column(column_6), .read_enable(read_enable),
    .data_out(latch_cell_7_data_out));
  latch_cell latch_cell_8 (
    .row(row), .write_enable(write_enable), .data_in(data_in), .column(column_7), .read_enable(read_enable),
    .data_out(latch_cell_8_data_out));
endmodule

module big_latch_row (
  input  column_8,
  input  column_9,
  input  read_enable,
  input  column_10,
  input  write_enable,
  input  column_11,
  input  column_12,
  input  column_13,
  input  column_14,
  input  column_0,
  input  column_15,
  input  column_1,
  input  column_2,
  input  data_in,
  input  column_3,
  input  row,
  input  column_4,
  input  column_5,
  input  column_6,
  input  column_7,
  output data_out
);

  wire latch_row_1_data_out, latch_row_2_data_out;

  latch_row latch_row_1 (
    .column_0(column_0), .column_1(column_1), .column_2(column_2), .column_3(column_3), .column_4(column_4),
    .column_5(column_5), .column_6(column_6), .column_7(column_7), .data_in(data_in),
    .write_enable(write_enable), .row(row), .read_enable(read_enable), .data_out(latch_row_1_data_out));
  or or_1 (data_out, latch_row_1_data_out, latch_row_2_data_out);
  latch_row latch_row_2 (
    .column_0(column_15), .column_1(column_14), .column_2(column_13), .column_3(column_12),
    .column_4(column_11), .column_5(column_10), .column_6(column_9), .column_7(column_8), .data_in(data_in),
    .write_enable(write_enable), .row(row), .read_enable(read_enable), .data_out(latch_row_2_data_out));
endmodule
